// Logisim project datapath.circ as structural Verilog: 5 circuits, main circuit my circuit
module my_circuit (
);

  wire ALUHi, ALULo, clock, CmpReg_q, comparison_logic_1_output, DrADDR, DrALU, DrMEM, DrOFF, DrPC, DrREG,
       LdA, LdB, LdCmp, LdIR, LdMAR, LdPC, RegSelHi, RegSelLo, WrMEM, WrREG;
  wire [3:0] CmpSel, regno;
  wire [19:0] IR_19_0;
  wire [23:0] MAR_q;
  wire [23:20] IR_23_0;
  wire [31:0] A_q, ALU_ouput, B_q, bit_extender_1_out, bit_extender_2_out, controlled_buffer_1_out, PC_q,
       ram_1_data, registers_1_ouput;
  wire [31:24] MAR_q_2;
  wire [31:28] IR_31_0;

  comparison_logic comparison_logic_1 (
    .bus(controlled_buffer_1_out), .\output (comparison_logic_1_output), .CmpSel(CmpSel));
  Register #(.width(32)) PC (.D(controlled_buffer_1_out), .en(LdPC), .Q(PC_q), .clk(clock));  // open: clr
  assign controlled_buffer_1_out = DrPC ? PC_q : 32'bz;  // Controlled_Buffer controlled_buffer_1
  Register #(.width(1)) CmpReg (.D(comparison_logic_1_output), .en(LdCmp), .Q(CmpReg_q), .clk(clock));  // open: clr
  Register #(.width(32)) A (.D(controlled_buffer_1_out), .en(LdA), .Q(A_q), .clk(clock));  // open: clr
  ALU ALU (.A(A_q), .B(B_q), .func({ALUHi, ALULo}), .ouput(ALU_ouput));
  assign controlled_buffer_1_out = DrALU ? ALU_ouput : 32'bz;  // Controlled_Buffer controlled_buffer_2
  Register #(.width(32)) B (.D(controlled_buffer_1_out), .en(LdB), .Q(B_q), .clk(clock));  // open: clr
  registers registers_1 (
    .WrREG(WrREG), .data(controlled_buffer_1_out), .regno(regno), .clock(clock), .ouput(registers_1_ouput));
  assign controlled_buffer_1_out = DrREG ? registers_1_ouput : 32'bz;  // Controlled_Buffer controlled_buffer_3
  microcontrol_unit microcontrol_unit_1 (
    .clock(clock), .CmpOut(CmpReg_q), .DrREG(DrREG), .DrMEM(DrMEM), .DrALU(DrALU), .DrPC(DrPC),
    .DrOFF(DrOFF), .DrADDR(DrADDR), .LdPC(LdPC), .LdIR(LdIR), .LdMAR(LdMAR), .LdA(LdA), .LdB(LdB),
    .LdCmp(LdCmp), .WrREG(WrREG), .WrMEM(WrMEM), .RegSelLo(RegSelLo), .RegSelHi(RegSelHi), .ALULo(ALULo),
    .ALUHi(ALUHi), .opcode(IR_31_0));
  Register #(.width(32)) MAR (.D(controlled_buffer_1_out), .en(LdMAR), .Q({MAR_q_2, MAR_q}), .clk(clock));  // open: clr
  assign controlled_buffer_1_out = DrMEM ? ram_1_data : 32'bz;  // Controlled_Buffer controlled_buffer_4
  RAM #(.addrWidth(24), .dataWidth(32), .bus("separate")) ram_1 (
    .addr(MAR_q), .din(controlled_buffer_1_out), .data(ram_1_data), .str(WrMEM), .clk(clock));  // open: sel, ld, clr
  assign controlled_buffer_1_out = DrOFF ? bit_extender_1_out : 32'bz;  // Controlled_Buffer controlled_buffer_5
  Clock clock_1 (.out(clock));
  Register #(.width(32)) IR (
    .D(controlled_buffer_1_out), .en(LdIR), .Q({IR_31_0, CmpSel, IR_23_0, IR_19_0}), .clk(clock));  // open: clr
  assign bit_extender_1_out = {{12{IR_19_0[19]}}, IR_19_0};  // Bit_Extender bit_extender_1
  Multiplexer #(.select(2), .width(4), .disabled(0), .enable("false")) multiplexer_1 (
    .in0(CmpSel), .in1(IR_23_0), .in2(IR_19_0[3:0]), .in3(4'b1111), .out(regno), .sel({RegSelHi, RegSelLo}));
  assign bit_extender_2_out = {{8{IR_23_0[23]}}, {IR_23_0, IR_19_0}};  // Bit_Extender bit_extender_2
  assign controlled_buffer_1_out = DrADDR ? bit_extender_2_out : 32'bz;  // Controlled_Buffer controlled_buffer_6

  // Other names for the same wires on the sheet: func[1:0] = {ALUHi, ALULo}; IR_23_0[19:0] = IR_19_0;
  //   IR_31_0[27:0] = {CmpSel, IR_23_0, IR_19_0}; RZ[3:0] = IR_19_0[3:0]; RY[3:0] = IR_23_0; RX[3:0] = CmpSel;
  //   OP[3:0] = IR_31_0
endmodule

module ALU (
  input  [31:0] A,
  input  [31:0] B,
  input  [1:0] func,
  output [31:0] ouput
);

  wire [31:0] adder_1_out, adder_2_out, nand_1_out, subtractor_1_out;

  Adder #(.width(32)) adder_1 (.a(A), .b(B), .out(adder_1_out));  // open: cin, cout
  Subtractor #(.width(32)) subtractor_1 (.a(A), .b(B), .out(subtractor_1_out));  // open: bin, bout
  Adder #(.width(32)) adder_2 (.a(A), .b(32'h1), .out(adder_2_out));  // open: cin, cout
  assign nand_1_out = ~(A & B);  // NAND_Gate nand_1, 32 bits wide
  Multiplexer #(.select(2), .width(32), .disabled(0), .enable("false")) multiplexer_1 (
    .in0(adder_1_out), .in1(subtractor_1_out), .in2(nand_1_out), .in3(adder_2_out), .out(ouput), .sel(func));
endmodule

module registers (
  input  [31:0] data,
  input  WrREG,
  input  clock,
  input  [3:0] regno,
  output [31:0] ouput
);

  wire we0, we1, we2, we3, we4, we5, we6, we7, we8, we9, we10, we11, we12, we13, we14, we15;
  wire [31:0] and_1_out, output0, output1, output2, output3, output4, output5, output6, output7, output8,
       output9, output10, output11, output12, output13, output14, output15;

  Demultiplexer #(.select(4), .disabled(0), .enable("false")) demultiplexer_1 (
    .out0(we0), .out1(we1), .out2(we2), .out3(we3), .out4(we4), .out5(we5), .out6(we6), .out7(we7),
    .out8(we8), .out9(we9), .out10(we10), .out11(we11), .out12(we12), .out13(we13), .out14(we14),
    .out15(we15), .in(WrREG), .sel(regno));
  assign and_1_out = data & {32{1'b0}};  // AND_Gate and_1, 32 bits wide
  Register #(.width(32)) register_1 (.D(and_1_out), .en(we0), .Q(output0), .clk(clock));  // open: clr
  Register #(.width(32)) register_2 (.D(data), .en(we4), .Q(output4), .clk(clock));  // open: clr
  Register #(.width(32)) register_3 (.D(data), .en(we8), .Q(output8), .clk(clock));  // open: clr
  Register #(.width(32)) register_4 (.D(data), .en(we12), .Q(output12), .clk(clock));  // open: clr
  Register #(.width(32)) register_5 (.D(data), .en(we1), .Q(output1), .clk(clock));  // open: clr
  Register #(.width(32)) register_6 (.D(data), .en(we5), .Q(output5), .clk(clock));  // open: clr
  Register #(.width(32)) register_7 (.D(data), .en(we9), .Q(output9), .clk(clock));  // open: clr
  Register #(.width(32)) register_8 (.D(data), .en(we13), .Q(output13), .clk(clock));  // open: clr
  Register #(.width(32)) register_9 (.D(data), .en(we2), .Q(output2), .clk(clock));  // open: clr
  Register #(.width(32)) register_10 (.D(data), .en(we6), .Q(output6), .clk(clock));  // open: clr
  Register #(.width(32)) register_11 (.D(data), .en(we10), .Q(output10), .clk(clock));  // open: clr
  Register #(.width(32)) register_12 (.D(data), .en(we14), .Q(output14), .clk(clock));  // open: clr
  Register #(.width(32)) register_13 (.D(data), .en(we3), .Q(output3), .clk(clock));  // open: clr
  Register #(.width(32)) register_14 (.D(data), .en(we7), .Q(output7), .clk(clock));  // open: clr
  Register #(.width(32)) register_15 (.D(data), .en(we11), .Q(output11), .clk(clock));  // open: clr
  Register #(.width(32)) register_16 (.D(data), .en(we15), .Q(output15), .clk(clock));  // open: clr
  Multiplexer #(.select(4), .width(32), .disabled(0), .enable("false")) multiplexer_1 (
    .in0(output0), .in1(output1), .in2(output2), .in3(output3), .in4(output4), .in5(output5), .in6(output6),
    .in7(output7), .in8(output8), .in9(output9), .in10(output10), .in11(output11), .in12(output12),
    .in13(output13), .in14(output14), .in15(output15), .out(ouput), .sel(regno));

  // Other names for the same wires on the sheet: output[31:0] = ouput
endmodule

module comparison_logic (
  input  [3:0] CmpSel,
  input  [31:0] bus,
  output \output 
);

  wire not_1_out, not_2_out, or_1_out, or_2_out, or_3_out, output1, output2;

  not not_1 (not_1_out, CmpSel[0]);
  and and_1 (output1, not_1_out, or_1_out);
  or or_1 (or_1_out, bus[31], bus[30], bus[29], bus[28], bus[27], bus[26], bus[25], bus[24], bus[23], bus[22], bus[21], bus[20], bus[19], bus[18], bus[17], bus[16], bus[15], bus[14], bus[13], bus[12], bus[11], bus[10], bus[9], bus[8], bus[7], bus[6], bus[5], bus[4], bus[3], bus[2], bus[1], bus[0]);
  xor xor_1 (\output , output1, output2);
  and and_2 (output2, CmpSel[0], or_2_out);
  or or_2 (or_2_out, bus[31], not_2_out);
  or or_3 (or_3_out, bus[31], bus[30], bus[29], bus[28], bus[27], bus[26], bus[25], bus[24], bus[23], bus[22], bus[21], bus[20], bus[19], bus[18], bus[17], bus[16], bus[15], bus[14], bus[13], bus[12], bus[11], bus[10], bus[9], bus[8], bus[7], bus[6], bus[5], bus[4], bus[3], bus[2], bus[1], bus[0]);
  not not_2 (not_2_out, or_3_out);

  // Other names for the same wires on the sheet: A_B[31:0] = bus; mode[3:0] = CmpSel
endmodule

module microcontrol_unit (
  input  [3:0] opcode,
  input  clock,
  input  CmpOut,
  output DrREG,
  output DrMEM,
  output DrALU,
  output DrPC,
  output DrOFF,
  output DrADDR,
  output LdPC,
  output LdIR,
  output LdMAR,
  output LdA,
  output LdB,
  output LdCmp,
  output WrREG,
  output WrMEM,
  output RegSelLo,
  output RegSelHi,
  output ALULo,
  output ALUHi
);

  wire [5:0] CmpReg_q, multiplexer_1_out, rom_2_data, rom_3_data;
  wire [25:0] rom_1_data;

  ROM #(.addrWidth(6), .dataWidth(26)) rom_1 (
    .addr(CmpReg_q),
    .data({rom_1_data[25:24], ALUHi, ALULo, RegSelHi, RegSelLo, WrMEM, WrREG, LdCmp, LdB, LdA, LdMAR, LdIR, LdPC, DrADDR, DrOFF, DrPC, DrALU, DrMEM, DrREG, rom_1_data[5:0]}));  // open: sel
  Register #(.width(6)) CmpReg (.D(multiplexer_1_out), .en(1'b1), .Q(CmpReg_q), .clk(clock));  // open: clr
  Multiplexer #(.select(2), .width(6), .disabled(0), .enable("false")) multiplexer_1 (
    .in0(rom_1_data[5:0]), .in1(rom_2_data), .in2(rom_3_data), .out(multiplexer_1_out),
    .sel(rom_1_data[25:24]));  // open: in3
  ROM #(.addrWidth(4), .dataWidth(6)) rom_2 (.addr(opcode), .data(rom_2_data));  // open: sel
  ROM #(.addrWidth(2), .dataWidth(6)) rom_3 (.addr({1'b0, CmpOut}), .data(rom_3_data));  // open: sel

  // Notes on the sheet:
  //   contents of rom_1 (hex, n*v repeats v):
  //   c201 2082 c01103 1000000 108045 210046 40100 108048 10409 40100 10804b 21004c 840100 10804e 21004f
  //   420110 2000000 8212 c01100 1800 40800 108056 10417 4118 40080 10805a 1041b 411c 80040 34021e 1040
  //   301040 20
  //   contents of rom_2 (hex, n*v repeats v):
  //   4 7 a d 13 14 0 0 15 19 0 0 1d 1f 0 20
  //   contents of rom_3 (hex, n*v repeats v):
  //   0 11
endmodule
