// Logisim project pipeline.circ as structural Verilog: 10 circuits, main circuit Dual-Ported Register File
module Dual_Ported_Register_File (
  input  CLK,
  input  WrEN,
  input  [3:0] WrREGNO,
  input  [3:0] RdREGNO1,
  input  [3:0] RdREGNO2,
  input  [31:0] INPUT,
  output [31:0] OUT1,
  output [31:0] OUT2
);

  wire En_a0, En_a1, En_a2, En_at, En_fp, En_k0, En_ra, En_s0, En_s1, En_s2, En_sp, En_t0, En_t1, En_t2,
       En_v0;
  wire [31:0] a0, a1, a2, at, fp, k0, ra, s0, s1, s2, sp, t0, t1, t2, v0, zero;

  Decoder #(.select(4), .disabled(0)) decoder_1 (
    .out1(En_at), .out2(En_v0), .out3(En_a0), .out4(En_a1), .out5(En_a2), .out6(En_t0), .out7(En_t1),
    .out8(En_t2), .out9(En_s0), .out10(En_s1), .out11(En_s2), .out12(En_k0), .out13(En_sp), .out14(En_fp),
    .out15(En_ra), .sel(WrREGNO), .en(WrEN));  // open: out0
  Register #(.width(32)) u_zero (.D(INPUT), .en(1'b0), .Q(zero), .clk(CLK));  // open: clr
  Register #(.width(32)) u_at (.D(INPUT), .en(En_at), .Q(at), .clk(CLK));  // open: clr
  Register #(.width(32)) u_v0 (.D(INPUT), .en(En_v0), .Q(v0), .clk(CLK));  // open: clr
  Register #(.width(32)) u_a0 (.D(INPUT), .en(En_a0), .Q(a0), .clk(CLK));  // open: clr
  Register #(.width(32)) u_a1 (.D(INPUT), .en(En_a1), .Q(a1), .clk(CLK));  // open: clr
  Register #(.width(32)) u_a2 (.D(INPUT), .en(En_a2), .Q(a2), .clk(CLK));  // open: clr
  Register #(.width(32)) u_t0 (.D(INPUT), .en(En_t0), .Q(t0), .clk(CLK));  // open: clr
  Register #(.width(32)) u_t1 (.D(INPUT), .en(En_t1), .Q(t1), .clk(CLK));  // open: clr
  Multiplexer #(.select(4), .width(32), .disabled(0), .enable("false")) multiplexer_1 (
    .in0(zero), .in1(at), .in2(v0), .in3(a0), .in4(a1), .in5(a2), .in6(t0), .in7(t1), .in8(t2), .in9(s0),
    .in10(s1), .in11(s2), .in12(k0), .in13(sp), .in14(fp), .in15(ra), .out(OUT2), .sel(RdREGNO2));
  Register #(.width(32)) u_t2 (.D(INPUT), .en(En_t2), .Q(t2), .clk(CLK));  // open: clr
  Register #(.width(32)) u_s0 (.D(INPUT), .en(En_s0), .Q(s0), .clk(CLK));  // open: clr
  Register #(.width(32)) u_s1 (.D(INPUT), .en(En_s1), .Q(s1), .clk(CLK));  // open: clr
  Register #(.width(32)) u_s2 (.D(INPUT), .en(En_s2), .Q(s2), .clk(CLK));  // open: clr
  Register #(.width(32)) u_k0 (.D(INPUT), .en(En_k0), .Q(k0), .clk(CLK));  // open: clr
  Register #(.width(32)) u_sp (.D(INPUT), .en(En_sp), .Q(sp), .clk(CLK));  // open: clr
  Register #(.width(32)) u_fp (.D(INPUT), .en(En_fp), .Q(fp), .clk(CLK));  // open: clr
  Register #(.width(32)) u_ra (.D(INPUT), .en(En_ra), .Q(ra), .clk(CLK));  // open: clr
  Multiplexer #(.select(4), .width(32), .disabled(0), .enable("false")) multiplexer_2 (
    .in0(zero), .in1(at), .in2(v0), .in3(a0), .in4(a1), .in5(a2), .in6(t0), .in7(t1), .in8(t2), .in9(s0),
    .in10(s1), .in11(s2), .in12(k0), .in13(sp), .in14(fp), .in15(ra), .out(OUT1), .sel(RdREGNO1));

  // Notes on the sheet:
  //   MODIFY AT YOUR OWN RISK
endmodule

module IF_IDRR_Buffer (
  input  cond,
  input  [31:0] BrPC,
  input  Clock,
  input  Stall,
  input  Flush,
  output [31:0] FBUF_IR,
  output [31:0] FBUF_PC
);

  wire en, HALT;
  wire [31:0] adder_1_out, multiplexer_1_out, multiplexer_2_out, multiplexer_3_out, PC_q, ram_1_data;

  Register #(.width(32)) PC (.D(multiplexer_2_out), .en(en), .Q(PC_q), .clk(Clock));  // open: clr
  Adder #(.width(32)) adder_1 (.a(PC_q), .b(32'h1), .out(adder_1_out));  // open: cin, cout
  Multiplexer #(.width(32), .disabled(0), .enable("false")) multiplexer_1 (
    .in0(adder_1_out), .in1(PC_q), .out(multiplexer_1_out), .sel(HALT));
  Multiplexer #(.width(32), .disabled(0), .enable("false")) multiplexer_2 (
    .in0(multiplexer_1_out), .in1(BrPC), .out(multiplexer_2_out), .sel(cond));
  RAM #(.addrWidth(24), .dataWidth(32)) ram_1 (.addr(PC_q[23:0]), .data(ram_1_data));  // open: sel, clk, ld, clr
  not not_1 (en, Stall);
  Comparator #(.width(32), .mode("unsigned")) comparator_1 (
    .a(32'hf0000000), .b(ram_1_data), .eq(HALT));  // open: gt, lt
  Multiplexer #(.width(32), .disabled(0), .enable("false")) multiplexer_3 (
    .in0(ram_1_data), .in1({32{1'b0}}), .out(multiplexer_3_out), .sel(Flush));
  Register #(.width(32)) register_1 (.D(multiplexer_1_out), .en(en), .Q(FBUF_PC), .clk(Clock));  // open: clr
  Register #(.width(32)) register_2 (.D(multiplexer_3_out), .en(en), .Q(FBUF_IR), .clk(Clock));  // open: clr
endmodule

module IDRR_EX_Buffer (
  input  [31:0] WBResult,
  input  [3:0] WBRx,
  input  [31:0] FBUF_PC,
  input  [31:0] newA,
  input  WtReg,
  input  [31:0] newB,
  input  [31:0] FBUF_IR,
  input  Clock,
  input  Stall,
  output [3:0] DBUF_Rx,
  output [31:0] DBUF_PCAddr24,
  output [3:0] DBUF_Opcode,
  output [31:0] DBUF_PC,
  output [31:0] DBUF_A,
  output [31:0] A,
  output [31:0] B,
  output [31:0] DBUF_B,
  output [3:0] SR2,
  output [31:0] DBUF_RxVal,
  output [3:0] SR1,
  output [31:0] BrPC,
  output Flush,
  output cond
);

  wire BrPCSel, BSel, comparator_1_eq, comparator_2_eq, comparator_3_eq, comparison_logic_1_cmp,
       multiplexer_9_out, RdRegSel;
  wire [3:0] multiplexer_2_out, multiplexer_4_out, multiplexer_5_out, multiplexer_6_out;
  wire [31:0] IR_19_0, multiplexer_8_out, multiplexer_10_out, multiplexer_11_out, PCaddr24;

  assign IR_19_0 = {{12{FBUF_IR[19]}}, FBUF_IR[19:0]};  // Bit_Extender bit_extender_1
  assign PCaddr24 = {{8{1'b0}}, FBUF_IR[23:0]};  // Bit_Extender bit_extender_2
  Multiplexer #(.disabled(0), .enable("false")) multiplexer_1 (.in0(WtReg), .in1(1'b0), .sel(Stall));  // open: out
  Multiplexer #(.width(4), .disabled(0), .enable("false")) multiplexer_2 (
    .in0(FBUF_IR[3:0]), .in1(FBUF_IR[27:24]), .out(multiplexer_2_out), .sel(RdRegSel));
  Comparator #(.width(4), .mode("unsigned")) comparator_1 (
    .a(FBUF_IR[31:28]), .b(4'b1101), .eq(comparator_1_eq));  // open: gt, lt
  Multiplexer #(.width(4), .disabled(0), .enable("false")) multiplexer_3 (
    .in0(multiplexer_2_out), .in1(4'b1111), .out(SR2), .sel(comparator_1_eq));
  ROM #(.addrWidth(4), .dataWidth(4)) rom_1 (
    .addr(FBUF_IR[31:28]), .data({cond, BrPCSel, BSel, RdRegSel}));  // open: sel
  Comparator #(.width(4), .mode("unsigned")) comparator_2 (
    .a(FBUF_IR[31:28]), .b(4'b1100), .eq(comparator_2_eq));  // open: gt, lt
  Multiplexer #(.width(4), .disabled(0), .enable("false")) multiplexer_4 (
    .in0(FBUF_IR[31:28]), .in1(4'b0000), .out(multiplexer_4_out), .sel(Stall));
  Multiplexer #(.width(4), .disabled(0), .enable("false")) multiplexer_5 (
    .in0(FBUF_IR[27:24]), .in1(4'b1111), .out(multiplexer_5_out), .sel(comparator_2_eq));
  Dual_Ported_Register_File dual_ported_register_file_1 (
    .CLK(Clock), .WrREGNO(WBRx), .RdREGNO1(FBUF_IR[23:20]), .RdREGNO2(SR2), .INPUT(WBResult), .OUT1(A),
    .OUT2(B), .WrEN(WtReg));
  Multiplexer #(.width(4), .disabled(0), .enable("false")) multiplexer_6 (
    .in0(multiplexer_5_out), .in1(4'b0000), .out(multiplexer_6_out), .sel(Stall));
  Register #(.width(4)) register_1 (.D(multiplexer_4_out), .Q(DBUF_Opcode), .clk(Clock));  // open: en, clr
  Register #(.width(4)) register_2 (.D(multiplexer_6_out), .Q(DBUF_Rx), .clk(Clock));  // open: en, clr
  Multiplexer #(.width(32), .disabled(0), .enable("false")) multiplexer_7 (
    .in0(PCaddr24), .in1(newB), .out(BrPC), .sel(BrPCSel));
  Register #(.width(32)) register_3 (.D(PCaddr24), .Q(DBUF_PCAddr24), .clk(Clock));  // open: en, clr
  Register #(.width(32)) register_4 (.D(FBUF_PC), .Q(DBUF_PC), .clk(Clock));  // open: en, clr
  Multiplexer #(.width(32), .disabled(0), .enable("false")) multiplexer_8 (
    .in0(newB), .in1(IR_19_0), .out(multiplexer_8_out), .sel(BSel));
  Comparison_Logic comparison_logic_1 (.SR1(newA), .SR2(newB), .mode(FBUF_IR[27:24]), .Cmp(comparison_logic_1_cmp));
  Comparator #(.width(4), .mode("unsigned")) comparator_3 (
    .a(FBUF_IR[31:28]), .b(4'b0011), .eq(comparator_3_eq));  // open: gt, lt
  Multiplexer #(.disabled(0), .enable("false")) multiplexer_9 (
    .in0(1'b0), .in1(comparison_logic_1_cmp), .out(multiplexer_9_out), .sel(comparator_3_eq));
  Multiplexer #(.width(32), .disabled(0), .enable("false")) multiplexer_10 (
    .in0(newA), .in1({32{1'b0}}), .out(multiplexer_10_out), .sel(Stall));
  Multiplexer #(.width(32), .disabled(0), .enable("false")) multiplexer_11 (
    .in0(multiplexer_8_out), .in1({32{1'b0}}), .out(multiplexer_11_out), .sel(Stall));
  Register #(.width(32)) register_5 (.D(newB), .Q(DBUF_RxVal), .clk(Clock));  // open: en, clr
  or or_1 (Flush, multiplexer_9_out, cond);
  Register #(.width(32)) register_6 (.D(multiplexer_10_out), .Q(DBUF_A), .clk(Clock));  // open: en, clr
  Register #(.width(32)) register_7 (.D(multiplexer_11_out), .Q(DBUF_B), .clk(Clock));  // open: en, clr

  assign SR1 = FBUF_IR[23:20];

  // Other names for the same wires on the sheet: JMP = cond; Rz[3:0] = FBUF_IR[3:0]; Ry[3:0] = FBUF_IR[23:20];
  //   Rx[3:0] = FBUF_IR[27:24]; opcode[3:0] = FBUF_IR[31:28]; NOOP = Stall

  // Notes on the sheet:
  //   contents of rom_1 (hex, n*v repeats v):
  //   0 2 0 0 8 0 0 0 2 3 0 0 d c
endmodule

module EX_MEM_Buffer (
  input  [3:0] DBUF_Opcode,
  input  [31:0] DBUF_A,
  input  [31:0] DBUF_B,
  input  Clock,
  input  [31:0] DBUF_PC,
  input  [31:0] DBUF_PCaddr24,
  input  [3:0] DBUF_Rx,
  input  [31:0] DBUF_RxVal,
  output [3:0] EXop,
  output [3:0] EBUF_Opcode,
  output Stall,
  output [31:0] EXResult,
  output [31:0] EBUF_Result,
  output [3:0] EXRx,
  output [3:0] EBUF_Rx,
  output [31:0] EBUF_RxVal
);

  wire CALL, func, LEA;
  wire [31:0] alu_1_aluresult;

  ALU alu_1 (.A(DBUF_A), .B(DBUF_B), .func(func), .ALUResult(alu_1_aluresult));
  Comparator #(.width(4), .mode("unsigned")) comparator_1 (.a(DBUF_Opcode), .b(4'b1100), .eq(CALL));  // open: gt, lt
  Comparator #(.width(4), .mode("unsigned")) comparator_2 (.a(DBUF_Opcode), .b(4'b0101), .eq(LEA));  // open: gt, lt
  Comparator #(.width(4), .mode("unsigned")) comparator_3 (.a(DBUF_Opcode), .b(4'b0010), .eq(func));  // open: gt, lt
  Comparator #(.width(4), .mode("unsigned")) comparator_4 (.a(DBUF_Opcode), .b(4'b1000), .eq(Stall));  // open: gt, lt
  Multiplexer #(.select(2), .width(32), .disabled(0), .enable("false")) multiplexer_1 (
    .in0(alu_1_aluresult), .in1(DBUF_PC), .in2(DBUF_PCaddr24), .out(EXResult), .sel({LEA, CALL}));  // open: in3
  Register #(.width(32)) register_1 (.D(EXResult), .Q(EBUF_Result), .clk(Clock));  // open: en, clr
  Register #(.width(4)) register_2 (.D(DBUF_Opcode), .Q(EBUF_Opcode), .clk(Clock));  // open: en, clr
  Register #(.width(4)) register_3 (.D(DBUF_Rx), .Q(EBUF_Rx), .clk(Clock));  // open: en, clr
  Register #(.width(32)) register_4 (.D(DBUF_RxVal), .Q(EBUF_RxVal), .clk(Clock));  // open: en, clr

  assign EXop = DBUF_Opcode;
  assign EXRx = DBUF_Rx;
endmodule

module MEM_WB_Buffer (
  input  [3:0] EBUF_Rx,
  input  [31:0] EBUF_Result,
  input  [31:0] EBUF_RxVal,
  input  Clock,
  input  [3:0] EBUF_Opcode,
  output [3:0] MEMRx,
  output [3:0] WBRx,
  output [31:0] WBResult,
  output [31:0] MEMResult,
  output [3:0] MEMop,
  output [3:0] WBop,
  output WtReg
);

  wire comparator_1_eq, comparator_2_eq;
  wire [31:0] ram_1_data;

  Comparator #(.width(4), .mode("unsigned")) comparator_1 (
    .a(4'b1001), .b(EBUF_Opcode), .eq(comparator_1_eq));  // open: gt, lt
  RAM #(.addrWidth(24), .dataWidth(32), .bus("separate")) ram_1 (
    .addr(EBUF_Result[23:0]), .din(EBUF_RxVal), .data(ram_1_data), .str(comparator_1_eq), .clk(Clock),
    .ld(1'b1));  // open: sel, clr
  Multiplexer #(.width(32), .disabled(0), .enable("false")) multiplexer_1 (
    .in0(EBUF_Result), .in1(ram_1_data), .out(MEMResult), .sel(comparator_2_eq));
  Comparator #(.width(4), .mode("unsigned")) comparator_2 (
    .a(4'b1000), .b(EBUF_Opcode), .eq(comparator_2_eq));  // open: gt, lt
  Register #(.width(4)) register_1 (.D(EBUF_Rx), .Q(WBRx), .clk(Clock));  // open: en, clr
  Register #(.width(32)) register_2 (.D(MEMResult), .Q(WBResult), .clk(Clock));  // open: en, clr
  Register #(.width(4)) register_3 (.D(EBUF_Opcode), .Q(WBop), .clk(Clock));  // open: en, clr
  WtReg wtreg_1 (.opcode(WBop), .WtReg(WtReg));

  assign MEMop = EBUF_Opcode;
  assign MEMRx = EBUF_Rx;
endmodule

module Forwarding_Unit (
  input  [3:0] SR1,
  input  [3:0] SR2,
  input  [3:0] EXRx,
  input  [3:0] MEMRx,
  input  [3:0] WBRx,
  input  [3:0] EXop,
  input  [3:0] MEMop,
  input  [3:0] WBop,
  input  [31:0] A,
  input  [31:0] B,
  input  [31:0] EXResult,
  input  [31:0] MEMResult,
  input  [31:0] WBResult,
  output [31:0] newA,
  output [31:0] newB
);

  wire and_1_out, and_2_out, and_3_out, and_4_out, and_5_out, and_6_out, comparator_1_eq, comparator_2_eq,
       comparator_3_eq, comparator_4_eq, comparator_5_eq, comparator_6_eq, comparator_7_eq, comparator_8_eq,
       wtreg_1_wtreg, wtreg_2_wtreg, wtreg_3_wtreg, wtreg_4_wtreg, wtreg_5_wtreg, wtreg_6_wtreg;
  wire [31:0] multiplexer_1_out, multiplexer_2_out, multiplexer_3_out, multiplexer_4_out, multiplexer_5_out,
       multiplexer_6_out;

  Comparator #(.width(4), .mode("unsigned")) comparator_1 (.a(SR1), .b(WBRx), .eq(comparator_1_eq));  // open: gt, lt
  Comparator #(.width(4), .mode("unsigned")) comparator_2 (.a(SR2), .b(WBRx), .eq(comparator_2_eq));  // open: gt, lt
  Comparator #(.width(4), .mode("unsigned")) comparator_3 (.a(SR2), .b(MEMRx), .eq(comparator_3_eq));  // open: gt, lt
  Comparator #(.width(4), .mode("unsigned")) comparator_4 (.a(SR2), .b(EXRx), .eq(comparator_4_eq));  // open: gt, lt
  Comparator #(.width(4), .mode("unsigned")) comparator_5 (.a(SR1), .b(MEMRx), .eq(comparator_5_eq));  // open: gt, lt
  Comparator #(.width(4), .mode("unsigned")) comparator_6 (.a(SR1), .b(EXRx), .eq(comparator_6_eq));  // open: gt, lt
  WtReg wtreg_1 (.opcode(WBop), .WtReg(wtreg_1_wtreg));
  and and_1 (and_1_out, comparator_1_eq, wtreg_2_wtreg);
  WtReg wtreg_2 (.opcode(WBop), .WtReg(wtreg_2_wtreg));
  WtReg wtreg_3 (.opcode(MEMop), .WtReg(wtreg_3_wtreg));
  WtReg wtreg_4 (.opcode(EXop), .WtReg(wtreg_4_wtreg));
  Comparator #(.width(4), .mode("unsigned")) comparator_7 (.a(SR1), .b(4'b0000), .eq(comparator_7_eq));  // open: gt, lt
  and and_2 (and_2_out, comparator_2_eq, wtreg_1_wtreg);
  and and_3 (and_3_out, comparator_3_eq, wtreg_5_wtreg);
  WtReg wtreg_5 (.opcode(MEMop), .WtReg(wtreg_5_wtreg));
  and and_4 (and_4_out, comparator_4_eq, wtreg_6_wtreg);
  WtReg wtreg_6 (.opcode(EXop), .WtReg(wtreg_6_wtreg));
  Multiplexer #(.width(32), .disabled(0), .enable("false")) multiplexer_1 (
    .in0(A), .in1(WBResult), .out(multiplexer_1_out), .sel(and_1_out));
  and and_5 (and_5_out, comparator_5_eq, wtreg_3_wtreg);
  Multiplexer #(.width(32), .disabled(0), .enable("false")) multiplexer_2 (
    .in0(multiplexer_1_out), .in1(MEMResult), .out(multiplexer_2_out), .sel(and_5_out));
  and and_6 (and_6_out, comparator_6_eq, wtreg_4_wtreg);
  Multiplexer #(.width(32), .disabled(0), .enable("false")) multiplexer_3 (
    .in0(B), .in1(WBResult), .out(multiplexer_3_out), .sel(and_2_out));
  Multiplexer #(.width(32), .disabled(0), .enable("false")) multiplexer_4 (
    .in0(multiplexer_3_out), .in1(MEMResult), .out(multiplexer_4_out), .sel(and_3_out));
  Multiplexer #(.width(32), .disabled(0), .enable("false")) multiplexer_5 (
    .in0(multiplexer_4_out), .in1(EXResult), .out(multiplexer_5_out), .sel(and_4_out));
  Comparator #(.width(4), .mode("unsigned")) comparator_8 (.a(SR2), .b(4'b0000), .eq(comparator_8_eq));  // open: gt, lt
  Multiplexer #(.width(32), .disabled(0), .enable("false")) multiplexer_6 (
    .in0(multiplexer_2_out), .in1(EXResult), .out(multiplexer_6_out), .sel(and_6_out));
  Multiplexer #(.width(32), .disabled(0), .enable("false")) multiplexer_7 (
    .in0(multiplexer_6_out), .in1(A), .out(newA), .sel(comparator_7_eq));
  Multiplexer #(.width(32), .disabled(0), .enable("false")) multiplexer_8 (
    .in0(multiplexer_5_out), .in1(B), .out(newB), .sel(comparator_8_eq));
endmodule

module ALU (
  input  [31:0] A,
  input  func,
  input  [31:0] B,
  output [31:0] ALUResult
);

  wire [31:0] adder_1_out, nand_1_out;

  Adder #(.width(32)) adder_1 (.a(A), .b(B), .out(adder_1_out));  // open: cin, cout
  assign nand_1_out = ~(A & B);  // NAND_Gate nand_1, 32 bits wide
  Multiplexer #(.width(32), .disabled(0), .enable("false")) multiplexer_1 (
    .in0(adder_1_out), .in1(nand_1_out), .out(ALUResult), .sel(func));
endmodule

module Comparison_Logic (
  input  [31:0] SR1,
  input  [31:0] SR2,
  input  [3:0] mode,
  output Cmp
);

  wire comparator_1_eq, comparator_1_gt, comparator_1_lt, or_1_out, or_2_out;

  Comparator #(.width(32)) comparator_1 (
    .a(SR1), .b(SR2), .gt(comparator_1_gt), .eq(comparator_1_eq), .lt(comparator_1_lt));
  or or_1 (or_1_out, comparator_1_lt, comparator_1_gt);
  Multiplexer #(.disabled(0), .enable("false")) multiplexer_1 (
    .in0(or_1_out), .in1(or_2_out), .out(Cmp), .sel(mode[0]));
  or or_2 (or_2_out, comparator_1_lt, comparator_1_eq);
endmodule

module WtReg (
  input  [3:0] opcode,
  output WtReg
);

  Multiplexer #(.select(4), .disabled(0), .enable("false")) multiplexer_1 (
    .in0(1'b1), .in1(1'b1), .in2(1'b1), .in3(1'b0), .in4(1'b0), .in5(1'b1), .in6(1'b0), .in7(1'b0),
    .in8(1'b1), .in9(1'b0), .in10(1'b0), .in11(1'b0), .in12(1'b1), .in13(1'b0), .in14(1'b0), .in15(1'b0),
    .out(WtReg), .sel(opcode));
endmodule

module main (
);

  wire Clock, cond, Flush, Stall, WtReg;
  wire [3:0] DBUF_Opcode, DBUF_Rx, EBUF_opcode, EBUF_Rx, EXop, EXRx, MEMop, MEMRx, SR1, SR2, WBop, WBRx;
  wire [31:0] A, B, BrPC, DBUF_A, DBUF_B, DBUF_PC, DBUF_PCadd24, DBUF_RxVal, EBUF_Result, EBUF_RxVal,
       EXResult, FBUF_IR, FBUF_PC, MEMResult, newA, newB, WBResult;

  IF_IDRR_Buffer if_idrr_buffer_1 (
    .BrPC(BrPC), .cond(cond), .Clock(Clock), .Stall(Stall), .Flush(Flush), .FBUF_IR(FBUF_IR),
    .FBUF_PC(FBUF_PC));
  Clock clock_1 (.out(Clock));
  IDRR_EX_Buffer idrr_ex_buffer_1 (
    .WBResult(WBResult), .WBRx(WBRx), .FBUF_PC(FBUF_PC), .WtReg(WtReg), .FBUF_IR(FBUF_IR), .A(A),
    .newA(newA), .Clock(Clock), .SR1(SR1), .SR2(SR2), .B(B), .Stall(Stall), .newB(newB), .BrPC(BrPC),
    .Flush(Flush), .cond(cond), .DBUF_Rx(DBUF_Rx), .DBUF_PCAddr24(DBUF_PCadd24), .DBUF_Opcode(DBUF_Opcode),
    .DBUF_PC(DBUF_PC), .DBUF_A(DBUF_A), .DBUF_B(DBUF_B), .DBUF_RxVal(DBUF_RxVal));
  Forwarding_Unit forwarding_unit_1 (
    .A(A), .B(B), .EXResult(EXResult), .MEMResult(MEMResult), .WBResult(WBResult), .SR1(SR1), .SR2(SR2),
    .EXRx(EXRx), .MEMRx(MEMRx), .WBRx(WBRx), .EXop(EXop), .MEMop(MEMop), .WBop(WBop), .newA(newA), .newB(newB));
  EX_MEM_Buffer ex_mem_buffer_1 (
    .DBUF_Opcode(DBUF_Opcode), .DBUF_A(DBUF_A), .DBUF_B(DBUF_B), .DBUF_PC(DBUF_PC),
    .DBUF_PCaddr24(DBUF_PCadd24), .DBUF_Rx(DBUF_Rx), .DBUF_RxVal(DBUF_RxVal), .EXop(EXop), .EXRx(EXRx),
    .Clock(Clock), .Stall(Stall), .EBUF_Opcode(EBUF_opcode), .EXResult(EXResult), .EBUF_Result(EBUF_Result),
    .EBUF_Rx(EBUF_Rx), .EBUF_RxVal(EBUF_RxVal));
  MEM_WB_Buffer mem_wb_buffer_1 (
    .EBUF_Rx(EBUF_Rx), .EBUF_Result(EBUF_Result), .EBUF_RxVal(EBUF_RxVal), .EBUF_Opcode(EBUF_opcode),
    .MEMop(MEMop), .MEMRx(MEMRx), .WBop(WBop), .Clock(Clock), .WBRx(WBRx), .WBResult(WBResult),
    .MEMResult(MEMResult), .WtReg(WtReg));
endmodule
